# Fritzing sketch CornholeKeep1 (saved by Fritzing 0.9.3b)
circuit board: 11.9701cm x 5.07935cm
breadboards: 1

parts:
  Radio = Adafruit RFM69HCW Transceiver Radio [part_number="Adafruit #3070 and #3071"]
  STATUS = LED - 5mm [color="Red (633nm)" package="5 mm [THT]"]
  Trinket_Pro = Adafruit Pro Trinket 5V 16MHz [part_number="Adafruit #2000"]
  R1 = Resistor [tolerance=±5% resistance=220 package=THT]
  CPart4 = Seven-Segment LED Backpack 1.2 Inch Digits [part_number=1269]
  SW2 = female pin header, 3 pins [form="♀ (female)"]
  SW1 = female pin header, 3 pins [form="♀ (female)"]
  RST = female pin header, 2 pins [form="♀ (female)"]
  7805 = Voltage Regulator [package=78xxl]
  C2 = Electrolytic Capacitor [capacitance=1µF package="100 mil [THT, electrolytic]"]
  C1 = Electrolytic Capacitor [capacitance=1µF package="100 mil [THT, electrolytic]"]
  PWR_SW = female pin header, 2 pins [form="♀ (female)"]
  BATT = 4xAA Switchable Battery Pack w/JST connector
  VCC1 = 4 x AAA Battery Mount  # not connected

nets:
  VIN: Radio.VIN, CPart4.VDD, CPart4.VCCIO, 7805.OUT, C2.+
  N1: Radio.EN, Trinket_Pro.A3
  N2: Radio.DIO0, Trinket_Pro.D3
  N3: Radio.SCK, Trinket_Pro.D13
  N4: Radio.MISO, Trinket_Pro.D11
  N5: Radio.MOSI, Trinket_Pro.D12
  N6: Radio.CS, Trinket_Pro.D10
  N7: STATUS.cathode, Trinket_Pro.GND#72, R1.Pin_0, R1.Pin_1, SW2.pin2, SW1.pin2, BATT.NEG
  N8: STATUS.anode, Trinket_Pro.D8
  N9: Trinket_Pro.VBAT, 7805.IN, C1.+, PWR_SW.pin1
  N10: Trinket_Pro.D6, SW2.pin3
  N11: Trinket_Pro.D5, SW2.pin1
  N12: Trinket_Pro.D4, SW1.pin3
  N13: Trinket_Pro.RESET, RST.pin2
  N14: Trinket_Pro.A0, SW1.pin1
  N15: Trinket_Pro.A4, CPart4.SDA
  N16: Trinket_Pro.A5, CPart4.SCL
  N17: 7805.GND, C2.-, C1.-
  N18: PWR_SW.pin2, BATT.POS

notes:
  CornholeKeep v0.1
  Joey Gennari 2017
  IO
  +
  -
  D
  C
  REV C

custom parts:
  Adafruit RFM69HCW Transceiver Radio: Sending data over long distances is like magic, and now you can be a magician with this range of powerful and easy-to-use radio modules. Sure, sometimes you want to talk to a computer (a good time to use WiFi) or perhaps communicate with a Phone (choose Bluetooth Low Energy!) but what if you want to send data very far? Most WiFi, Bluetooth, Zigbee and other wireless chipsets use 2.4GHz, which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
  Adafruit Pro Trinket 5V 16MHz: Trinket's got a big sister in town - the Pro Trinket 5V! Pro Trinket combines everything you love about Trinket with the familiarity of the common core Arduino chip, the ATmega328. It's like an Arduino Pro Mini with more pins and USB tossed in, so delicious. Trinket's a year old now, and while its been great to see tons of tiny projects, sometimes you just need more pins, more FLASH, and more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
  Seven-Segment LED Backpack 1.2 Inch Digits: This jumbo 1.2" 7-segment LED display includes a driver chip for simple control via an I2C interface. The backpack features address-selection jumpers so you can connect up to eight displays on a single I2C bus.
  4xAA Switchable Battery Pack w/JST connector: 4xAA Switchable Battery Pack with JST connector
