# Fritzing sketch CornholeKeep2 (saved by Fritzing 0.9.3b)
circuit board: 11.9973cm x 5.79577cm
breadboards: 1

parts:
  RFM69HCW = Adafruit RFM69HCW Transceiver Radio [part_number="Adafruit #3070 and #3071"]
  CPart4 = Seven-Segment LED Backpack 1.2 Inch Digits [part_number=1269]
  RST = female pin header, 2 pins [form="♀ (female)"]
  PWR_SW = female pin header, 2 pins [form="♀ (female)"]
  SW1 = Generic female header - 3 pins [form="♀ (female)" package=THT]
  SW2 = Generic female header - 3 pins [form="♀ (female)" package=THT]
  STATUS = smd LED [color="Red (633nm)" package="0805 [SMD]"]
  R2 = 220 Ω Resistor [package="0805 [SMD]"]
  5V_Reg = Generic female header - 3 pins [form="♀ (female)" package=THT]
  4xAAA = 4 x AAA Battery Mount
  SPK = Piezo Speaker
  Trinket_Pro_5v = Adafruit Pro Trinket 5V 16MHz [part_number="Adafruit #2000"]
  5V_Brd = female pin header, 1 pin [form="♀ (female)"]

nets:
  N1: RFM69HCW.VIN, PWR_SW.pin1, 5V_Reg.pin3, Trinket_Pro_5v.VBAT
  N2: RFM69HCW.EN, Trinket_Pro_5v.A0
  N3: RFM69HCW.DIO0, Trinket_Pro_5v.D3
  N4: RFM69HCW.SCK, Trinket_Pro_5v.D13
  N5: RFM69HCW.MISO, Trinket_Pro_5v.D11
  N6: RFM69HCW.MOSI, Trinket_Pro_5v.D12
  N7: RFM69HCW.CS, Trinket_Pro_5v.D10
  N8: RFM69HCW.RST, Trinket_Pro_5v.D9
  N9: CPart4.SCL, Trinket_Pro_5v.A5
  N10: CPart4.SDA, Trinket_Pro_5v.A4
  N11: CPart4.VDD, CPart4.VCCIO, 5V_Reg.pin1
  N12: RST.pin2, Trinket_Pro_5v.RESET
  N13: PWR_SW.pin2, 4xAAA.+
  N14: SW1.pin1, Trinket_Pro_5v.A2
  N15: SW1.pin3, Trinket_Pro_5v.D4
  N16: SW2.pin1, Trinket_Pro_5v.D5
  N17: SW2.pin3, Trinket_Pro_5v.D6
  N18: STATUS.cathode, R2.Pin_0
  N19: STATUS.anode, Trinket_Pro_5v.D8
  GND: R2.GND
  N20: SPK.pin1, Trinket_Pro_5v.A1
  N21: Trinket_Pro_5v.+5V, 5V_Brd.pin1

notes:
  ScoreKeepr v0.1
  Joey Gennari 2017
  IO
  +
  -
  D
  C
  REV C
  Radio
  Trinket Pro 5v

custom parts:
  Adafruit RFM69HCW Transceiver Radio: Sending data over long distances is like magic, and now you can be a magician with this range of powerful and easy-to-use radio modules. Sure, sometimes you want to talk to a computer (a good time to use WiFi) or perhaps communicate with a Phone (choose Bluetooth Low Energy!) but what if you want to send data very far? Most WiFi, Bluetooth, Zigbee and other wireless chipsets use 2.4GHz, which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
  Seven-Segment LED Backpack 1.2 Inch Digits: This jumbo 1.2" 7-segment LED display includes a driver chip for simple control via an I2C interface. The backpack features address-selection jumpers so you can connect up to eight displays on a single I2C bus.
  Generic female header - 3 pins: Generic female header
  220 Ω Resistor: A generic resistor
  Adafruit Pro Trinket 5V 16MHz: Trinket's got a big sister in town - the Pro Trinket 5V! Pro Trinket combines everything you love about Trinket with the familiarity of the common core Arduino chip, the ATmega328. It's like an Arduino Pro Mini with more pins and USB tossed in, so delicious. Trinket's a year old now, and while its been great to see tons of tiny projects, sometimes you just need more pins, more FLASH, and more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
